// Logisim project CT8.circ as structural Verilog: 4 circuits, main circuit main
module main (
);

  wire [7:0] alu_1_out_7, instrreg_1_out_5, regs_1_dout, regs_2_dout;

  regs regs_1 (.Din(alu_1_out_7), .Dout(regs_1_dout));  // open: WE, Clck, Rst, OE
  regs regs_2 (.Din(alu_1_out_7), .Dout(regs_2_dout));  // open: WE, Clck, Rst, OE
  instrReg instrreg_1 (.out_5(instrreg_1_out_5));  // open: WE, instIn, Clck, Rst
  ALU alu_1 (.A(regs_1_dout), .B(regs_2_dout), .out_7(alu_1_out_7));  // open: CEnbl, Cin, OP, OutEn, COut, Z, N, V
endmodule

module ALU (
  input  CEnbl,
  input  Cin,
  input  [7:0] A,
  input  [7:0] B,
  input  [2:0] OP,
  input  OutEn,
  output [7:0] out_7,
  output COut,
  output Z,
  output N,
  output V
);

  wire adder_1_cout, and_1_out, and_3_out, decoder_1_out0, decoder_1_out2, decoder_1_out3, decoder_1_out4,
       decoder_1_out5, nor_1_out, not_2_out, xor_2_out, xor_3_out, xor_5_out, xor_6_out;
  wire [7:0] adder_1_out, and_2_out, controlled_buffer_1_out, not_1_out, or_1_out, xor_1_out, xor_4_out;
  wire [7:7] decoder_1_out1;

  // Probe on A
  // Probe on B
  assign xor_1_out = B ^ {8{decoder_1_out1[7]}};  // XOR_Gate xor_1, 8 bits wide
  Decoder #(.select(3)) decoder_1 (
    .out0(decoder_1_out0), .out1(decoder_1_out1[7]), .out2(decoder_1_out2), .out3(decoder_1_out3),
    .out4(decoder_1_out4), .out5(decoder_1_out5), .sel(OP), .en(1'b1));  // open: out6, out7
  and and_1 (and_1_out, CEnbl, Cin);
  xor xor_2 (xor_2_out, and_1_out, decoder_1_out1[7]);
  xor xor_3 (xor_3_out, decoder_1_out1[7], decoder_1_out0);
  assign controlled_buffer_1_out = xor_3_out ? adder_1_out : 8'bz;  // Controlled_Buffer controlled_buffer_1
  Adder adder_1 (.a(A), .b(xor_1_out), .out(adder_1_out), .cin(xor_2_out), .cout(adder_1_cout));
  assign and_2_out = A & xor_1_out;  // AND_Gate and_2, 8 bits wide
  assign controlled_buffer_1_out = decoder_1_out2 ? and_2_out : 8'bz;  // Controlled_Buffer controlled_buffer_2
  assign or_1_out = A | xor_1_out;  // OR_Gate or_1, 8 bits wide
  assign controlled_buffer_1_out = decoder_1_out3 ? or_1_out : 8'bz;  // Controlled_Buffer controlled_buffer_3
  assign xor_4_out = A ^ xor_1_out;  // XOR_Gate xor_4, 8 bits wide
  assign controlled_buffer_1_out = decoder_1_out4 ? xor_4_out : 8'bz;  // Controlled_Buffer controlled_buffer_4
  assign not_1_out = ~A;  // NOT_Gate not_1, 8 bits wide
  assign controlled_buffer_1_out = decoder_1_out5 ? not_1_out : 8'bz;  // Controlled_Buffer controlled_buffer_5
  xor xor_5 (xor_5_out, controlled_buffer_1_out[7], A[7]);
  xor xor_6 (xor_6_out, A[7], B[7]);
  not not_2 (not_2_out, xor_6_out);
  nor nor_1 (nor_1_out, controlled_buffer_1_out[0], controlled_buffer_1_out[1], controlled_buffer_1_out[2], controlled_buffer_1_out[3], controlled_buffer_1_out[4], controlled_buffer_1_out[5], controlled_buffer_1_out[6], controlled_buffer_1_out[7]);
  and and_3 (and_3_out, xor_5_out, not_2_out);
  assign out_7 = OutEn ? controlled_buffer_1_out : 8'bz;  // Controlled_Buffer controlled_buffer_6
  assign COut = OutEn ? adder_1_cout : 1'bz;  // Controlled_Buffer controlled_buffer_7
  assign Z = OutEn ? nor_1_out : 1'bz;  // Controlled_Buffer controlled_buffer_8
  assign N = OutEn ? controlled_buffer_1_out[7] : 1'bz;  // Controlled_Buffer controlled_buffer_9
  assign V = OutEn ? and_3_out : 1'bz;  // Controlled_Buffer controlled_buffer_10
  // Probe on controlled_buffer_1_out
endmodule

module regs (
  input  [7:0] Din,
  input  WE,
  input  Clck,
  input  Rst,
  input  OE,
  output [7:0] Dout
);

  wire [7:0] register_1_q;

  Register register_1 (.D(Din), .en(WE), .clk(Clck), .Q(register_1_q), .clr(Rst));
  assign Dout = OE ? register_1_q : 8'bz;  // Controlled_Buffer controlled_buffer_1
endmodule

module instrReg (
  input  [7:0] instIn,
  input  WE,
  input  Clck,
  input  Rst,
  output [7:0] out_5
);

  Register register_1 (.D(instIn), .en(WE), .clk(Clck), .Q(out_5), .clr(Rst));
endmodule
